# Fritzing sketch pomodoro-timer (saved by Fritzing 0.9.9b)
breadboards: 1

parts:
  J1 = STM32 Nucleo boards
  Part1 = OLED Monochrome 128x64 0.96 inch [part_number=326]

nets:
  N1: J1.D10_PWM/SS, Part1.CS
  GND: J1.GND, Part1.GND
  N2: J1.A4/SDA, Part1.MOSI_SDA
  N3: J1.A5/SCL, Part1.SCLK_SCK
  3V3: J1.3V3, Part1.VIN

custom parts:
  OLED Monochrome 128x64 0.96 inch: These displays are small, only about 1" diameter, but very readable due to the high contrast of an OLED display. This display is made of 128x64 individual white OLED pixels, each one is turned on or off by the controller chip. Because the display makes its own light, no backlight is required. This reduces the power required to run the OLED and is why the display has such high contrast; we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
